// Logisim project pipeline.circ as structural Verilog: 7 circuits, main circuit main
module main (
);

  wire B, CLK, control_1_memwrite, DepRA1, DepRA3, DepRA4, DepRB1, DepRB3, DepRB4, equal_1_s, equal_2_s,
       IMMSRC_C, IMMSRC_D, LOCK, multiplexer_5_out, multiplexer_6_out, multiplexer_7_out, multiplexer_8_out,
       multiplexer_16_out, multiplexer_17_out, multiplexer_18_out, not_1_out, or_2_out, or_3_out, R,
       register_15_q, register_16_q, register_17_q, register_18_q, register_30_q, register_31_q,
       register_32_q, W1, W3, W4, zero_1_zero;
  wire [1:0] and_1_out, control_1_mov, MOV, multiplexer_1_out, not_2_out, or_1_out, PCSRC, register_34_q,
       register_35_q, register_36_q, Z;
  wire [2:0] control_1_ulaout3, control_1_ulaout4, ULA3, ULA4;
  wire [3:0] RA_RB1, RA_RB3, RA_RB4, register_4_q, register_5_q, register_7_q, register_10_q, register_13_q,
       register_21_q, register_22_q, register_23_q;
  wire [3:2] register_3_q;
  wire [7:0] adder_1_out, adder_2_out, IMM1, IMM2, multiplexer_2_out, multiplexer_4_out, multiplexer_9_out,
       multiplexer_10_out, multiplexer_11_out, multiplexer_12_out, multiplexer_13_out, multiplexer_14_out,
       multiplexer_15_out, multiplexer_19_out, ram_1_dout, register_1_q, register_24_q, register_25_q,
       register_26_q, register_27_q, register_28_q, register_29_q, register_33_q, register_37_q,
       register_38_q, registers_1_sra1, registers_1_sra2, registers_1_sra3, registers_1_sra4,
       registers_1_srb1, registers_1_srb3, registers_1_srb4, shifter_1_out, shifter_2_out, SRA1, SRA3, SRA4,
       SRB1, SRB2, SRB3, SRB4, subtractor_1_out, ula_1_ulares, ula_2_ulares, undriven, undriven_2,
       undriven_3, undriven_4;
  wire [31:0] multiplexer_3_out;

  Subtractor subtractor_1 (.a(IMM2), .b(8'h1), .out(subtractor_1_out));  // open: bin, bout
  Shifter shifter_1 (.in(subtractor_1_out), .\dist (3'b010), .out(shifter_1_out));
  assign and_1_out = PCSRC & Z;  // AND_Gate and_1, 2 bits wide
  Adder adder_1 (.a(register_1_q), .b(8'h4), .out(adder_1_out));  // open: cin, cout
  Adder adder_2 (.a(register_1_q), .b(shifter_1_out), .out(adder_2_out));  // open: cin, cout
  Shifter shifter_2 (.in(SRB2), .\dist (3'b010), .out(shifter_2_out));
  Multiplexer #(.width(2)) multiplexer_1 (.in0(PCSRC), .in1(and_1_out), .out(multiplexer_1_out), .sel(B));
  assign or_1_out = multiplexer_1_out | {2{LOCK}};  // OR_Gate or_1, 2 bits wide
  Register register_1 (.D(multiplexer_2_out), .en(1'b1), .clk(CLK), .Q(register_1_q), .clr(R));
  Multiplexer #(.select(2), .width(8)) multiplexer_2 (
    .in0(adder_1_out), .in1(adder_2_out), .in2(shifter_2_out), .in3(register_1_q), .out(multiplexer_2_out),
    .sel(or_1_out));
  // ROM #(.line("quad")) rom_1: pin names not known; wires that end beside it: register_1_q
  Clock clock_1 (.out(CLK));
  Button button_1 (.out(R));
  equal equal_1 (.E1(2'b10), .E2(or_1_out), .S(equal_1_s));
  equal equal_2 (.E1(2'b01), .E2(or_1_out), .S(equal_2_s));
  or or_2 (or_2_out, equal_2_s, equal_1_s, R);
  Multiplexer #(.width(32)) multiplexer_3 (
    .in0({undriven_4, undriven_3, undriven_2, undriven}), .in1({32{1'b1}}), .out(multiplexer_3_out),
    .sel(or_2_out));
  not not_1 (not_1_out, LOCK);
  Register #(.width(2)) register_2 (.D(multiplexer_3_out[1:0]), .en(not_1_out), .Q(RA_RB1[1:0]), .clk(CLK), .clr(1'b0));
  Register #(.width(2)) register_3 (
    .D(multiplexer_3_out[3:2]), .en(not_1_out), .Q(register_3_q), .clk(CLK), .clr(1'b0));
  Register #(.width(4)) register_4 (
    .D(multiplexer_3_out[7:4]), .en(not_1_out), .Q(register_4_q), .clk(CLK), .clr(1'b0));
  Register #(.width(2)) register_5 (
    .D(multiplexer_3_out[9:8]), .en(not_1_out), .Q(register_5_q[1:0]), .clk(CLK), .clr(1'b0));
  Register #(.width(2)) register_6 (
    .D(multiplexer_3_out[11:10]), .en(not_1_out), .Q(register_5_q[3:2]), .clk(CLK), .clr(1'b0));
  Register #(.width(4)) register_7 (
    .D(multiplexer_3_out[15:12]), .en(not_1_out), .Q(register_7_q), .clk(CLK), .clr(1'b0));
  Register #(.width(2)) register_8 (
    .D(multiplexer_3_out[17:16]), .en(not_1_out), .Q(RA_RB3[1:0]), .clk(CLK), .clr(1'b0));
  Register #(.width(2)) register_9 (
    .D(multiplexer_3_out[19:18]), .en(not_1_out), .Q(RA_RB3[3:2]), .clk(CLK), .clr(1'b0));
  Register #(.width(4)) register_10 (
    .D(multiplexer_3_out[23:20]), .en(not_1_out), .Q(register_10_q), .clk(CLK), .clr(1'b0));
  Register #(.width(2)) register_11 (
    .D(multiplexer_3_out[25:24]), .en(not_1_out), .Q(RA_RB4[1:0]), .clk(CLK), .clr(1'b0));
  Register #(.width(2)) register_12 (
    .D(multiplexer_3_out[27:26]), .en(not_1_out), .Q(RA_RB4[3:2]), .clk(CLK), .clr(1'b0));
  Register #(.width(4)) register_13 (
    .D(multiplexer_3_out[31:28]), .en(not_1_out), .Q(register_13_q), .clk(CLK), .clr(1'b0));
  assign RA_RB1[3:2] = register_3_q & not_2_out;  // AND_Gate and_2, 2 bits wide
  assign IMM2 = {{4{register_5_q[3]}}, register_5_q};  // Bit_Extender bit_extender_1
  assign IMM1 = {{4{register_3_q[3]}}, {register_3_q, RA_RB1[1:0]}};  // Bit_Extender bit_extender_2
  assign not_2_out = ~{2{IMMSRC_D}};  // NOT_Gate not_2, 2 bits wide
  registers registers_1 (
    .B(B), .IMMSRC_C(IMMSRC_C), .RA2(register_5_q[3:2]), .RA1(RA_RB1[3:2]), .RA3(RA_RB3[3:2]),
    .RA4(RA_RB4[3:2]), .RB1(RA_RB1[1:0]), .RB2(register_5_q[1:0]), .RB3(RA_RB3[1:0]), .RB4(RA_RB4[1:0]),
    .RA1WB(register_34_q), .RA3WB(register_35_q), .RA4WB(register_36_q), .WB4(register_32_q),
    .WB3(register_31_q), .WB1(register_30_q), .DATA3(register_37_q), .DATA1(register_33_q),
    .DATA4(register_38_q), .REGW1(W1), .REGW3(W3), .REGW4(W4), .R(R), .CLK(CLK), .SRA1(registers_1_sra1),
    .SRB1(registers_1_srb1), .SRA2(registers_1_sra2), .SRB2(SRB2), .SRA3(registers_1_sra3),
    .SRB3(registers_1_srb3), .SRA4(registers_1_sra4), .SRB4(registers_1_srb4), .L(LOCK));
  control control_1 (
    .OPCODE4(register_13_q), .OPCODE1(register_4_q), .OPCODE2(register_7_q), .OPCODE3(register_10_q),
    .ULAOUT4(control_1_ulaout4), .REGW4(W4), .MOV(control_1_mov), .IMMSRC_D(IMMSRC_D), .REGW1(W1),
    .MEMWRITE(control_1_memwrite), .PCSRC(PCSRC), .IMMSRC_C(IMMSRC_C), .B(B), .ULAOUT3(control_1_ulaout3),
    .REGW3(W3));
  or or_3 (or_3_out, LOCK, R);
  Multiplexer #(.width(8)) multiplexer_4 (.in0(registers_1_srb1), .in1(IMM1), .out(multiplexer_4_out), .sel(IMMSRC_D));
  assign Z = {{1{zero_1_zero}}, zero_1_zero};  // Bit_Extender bit_extender_3
  Zero zero_1 (.S(registers_1_sra2), .Zero(zero_1_zero));
  Multiplexer multiplexer_5 (.in0(W1), .in1(1'b0), .out(multiplexer_5_out), .sel(or_3_out));
  Multiplexer multiplexer_6 (.in0(W3), .in1(1'b0), .out(multiplexer_6_out), .sel(or_3_out));
  Multiplexer multiplexer_7 (.in0(W4), .in1(1'b0), .out(multiplexer_7_out), .sel(or_3_out));
  Multiplexer multiplexer_8 (.in0(control_1_memwrite), .in1(1'b0), .out(multiplexer_8_out), .sel(or_3_out));
  Register #(.width(2)) register_14 (.D(control_1_mov), .en(1'b1), .Q(MOV), .clk(CLK), .clr(1'b0));
  Register #(.width(1)) register_15 (.D(multiplexer_5_out), .en(1'b1), .Q(register_15_q), .clk(CLK), .clr(1'b0));
  Register #(.width(1)) register_16 (.D(multiplexer_6_out), .en(1'b1), .Q(register_16_q), .clk(CLK), .clr(1'b0));
  Register #(.width(1)) register_17 (.D(multiplexer_7_out), .en(1'b1), .Q(register_17_q), .clk(CLK), .clr(1'b0));
  Register #(.width(1)) register_18 (.D(multiplexer_8_out), .en(1'b1), .Q(register_18_q), .clk(CLK), .clr(1'b0));
  Register #(.width(3)) register_19 (.D(control_1_ulaout3), .en(1'b1), .Q(ULA3), .clk(CLK), .clr(1'b0));
  Register #(.width(3)) register_20 (.D(control_1_ulaout4), .en(1'b1), .Q(ULA4), .clk(CLK), .clr(1'b0));
  Register #(.width(4)) register_21 (.D(RA_RB1), .en(1'b1), .Q(register_21_q), .clk(CLK), .clr(1'b0));
  Register #(.width(4)) register_22 (.D(RA_RB3), .en(1'b1), .Q(register_22_q), .clk(CLK), .clr(1'b0));
  Register #(.width(4)) register_23 (.D(RA_RB4), .en(1'b1), .Q(register_23_q), .clk(CLK), .clr(1'b0));
  Register register_24 (.D(registers_1_sra1), .en(1'b1), .Q(register_24_q), .clk(CLK), .clr(1'b0));
  Register register_25 (.D(multiplexer_4_out), .en(1'b1), .Q(register_25_q), .clk(CLK), .clr(1'b0));
  Register register_26 (.D(registers_1_sra3), .en(1'b1), .Q(register_26_q), .clk(CLK), .clr(1'b0));
  Register register_27 (.D(registers_1_srb3), .en(1'b1), .Q(register_27_q), .clk(CLK), .clr(1'b0));
  Register register_28 (.D(registers_1_sra4), .en(1'b1), .Q(register_28_q), .clk(CLK), .clr(1'b0));
  Register register_29 (.D(registers_1_srb4), .en(1'b1), .Q(register_29_q), .clk(CLK), .clr(1'b0));
  Multiplexer #(.width(8)) multiplexer_9 (.in0(register_24_q), .in1(SRA1), .out(multiplexer_9_out), .sel(DepRA1));
  RAM #(.trigger("falling")) ram_1 (
    .addr(multiplexer_10_out), .we(register_18_q), .oe(1'b1), .clk(CLK), .din(multiplexer_9_out),
    .dout(ram_1_dout));
  Multiplexer #(.width(8)) multiplexer_10 (.in0(register_25_q), .in1(SRB1), .out(multiplexer_10_out), .sel(DepRB1));
  Multiplexer #(.width(8)) multiplexer_11 (.in0(register_26_q), .in1(SRA3), .out(multiplexer_11_out), .sel(DepRA3));
  Multiplexer #(.width(8)) multiplexer_12 (.in0(register_27_q), .in1(SRB3), .out(multiplexer_12_out), .sel(DepRB3));
  Multiplexer #(.width(8)) multiplexer_13 (.in0(register_28_q), .in1(SRA4), .out(multiplexer_13_out), .sel(DepRA4));
  Multiplexer #(.width(8)) multiplexer_14 (.in0(register_29_q), .in1(SRB4), .out(multiplexer_14_out), .sel(DepRB4));
  Multiplexer #(.width(8)) multiplexer_15 (
    .in0({register_25_q[3:0], multiplexer_9_out[3:0]}), .in1({multiplexer_9_out[7:4], register_25_q[3:0]}),
    .out(multiplexer_15_out), .sel(MOV[0]));
  Multiplexer multiplexer_16 (.in0(register_15_q), .in1(1'b0), .out(multiplexer_16_out), .sel(R));
  Register #(.width(1)) register_30 (.D(multiplexer_16_out), .en(1'b1), .Q(register_30_q), .clk(CLK), .clr(1'b0));
  Multiplexer multiplexer_17 (.in0(register_16_q), .in1(1'b0), .out(multiplexer_17_out), .sel(R));
  Register #(.width(1)) register_31 (.D(multiplexer_17_out), .en(1'b1), .Q(register_31_q), .clk(CLK), .clr(1'b0));
  Multiplexer multiplexer_18 (.in0(register_17_q), .in1(1'b0), .out(multiplexer_18_out), .sel(R));
  Register #(.width(1)) register_32 (.D(multiplexer_18_out), .en(1'b1), .Q(register_32_q), .clk(CLK), .clr(1'b0));
  Multiplexer #(.width(8)) multiplexer_19 (
    .in0(ram_1_dout), .in1(multiplexer_15_out), .out(multiplexer_19_out), .sel(MOV[1]));
  Register register_33 (.D(multiplexer_19_out), .en(1'b1), .Q(register_33_q), .clk(CLK), .clr(1'b0));
  Register #(.width(2)) register_34 (.D(register_21_q[3:2]), .en(1'b1), .Q(register_34_q), .clk(CLK), .clr(1'b0));
  Register #(.width(2)) register_35 (.D(register_22_q[3:2]), .en(1'b1), .Q(register_35_q), .clk(CLK), .clr(1'b0));
  Register #(.width(2)) register_36 (.D(register_23_q[3:2]), .en(1'b1), .Q(register_36_q), .clk(CLK), .clr(1'b0));
  ula ula_1 (.ULAOUT(ULA3), .RAOUT(multiplexer_11_out), .RBOUT(multiplexer_12_out), .ULARES(ula_1_ulares));
  Register register_37 (.D(ula_1_ulares), .en(1'b1), .Q(register_37_q), .clk(CLK), .clr(1'b0));
  ula ula_2 (.ULAOUT(ULA4), .RAOUT(multiplexer_13_out), .RBOUT(multiplexer_14_out), .ULARES(ula_2_ulares));
  Register register_38 (.D(ula_2_ulares), .en(1'b1), .Q(register_38_q), .clk(CLK), .clr(1'b0));
  forwardingUnit forwardingunit_1 (
    .WRA1_A(register_30_q), .WRA3_A(register_31_q), .WRA4_A(register_32_q), .RA1_A(register_34_q),
    .RA3_A(register_35_q), .RA4_A(register_36_q), .RB1_B(register_21_q[1:0]), .RB3_B(register_22_q[1:0]),
    .RB4_B(register_23_q[1:0]), .RA1_B(register_21_q[3:2]), .RA3_B(register_22_q[3:2]),
    .RA4_B(register_23_q[3:2]), .SRA1_A(register_33_q), .SRA3_A(register_37_q), .SRA4_A(register_38_q),
    .DepRB1(DepRB1), .SRB1(SRB1), .DepRB3(DepRB3), .SRB3(SRB3), .DepRB4(DepRB4), .SRB4(SRB4),
    .DepRA1(DepRA1), .SRA1(SRA1), .DepRA3(DepRA3), .SRA3(SRA3), .DepRA4(DepRA4), .SRA4(SRA4));

  // Notes on the sheet:
  //   contents of rom_1 (hex, n*v repeats v):
  //   61 ff 95 9a 77 ff 9f ff 7f ff 84 ff 60 ff 88 ff 71 ff ff ff 7b ff 8c ff 59 ff 9b ff 50 12 ff ff ff
  //   3e 93 97 7b ff d7 9a 59 12 87 ff ff 3f 93 ff 61 ff 9a 9f 77 ff 95 ff 60 ff 88 8c 7c ff ff ff 7b ff
  //   84 ff 4a 5*ff 82 9a ff 32 ff ff ff 3d 4*ff 8b 8d 53 ff 90 9f 71 5*ff 8c 90 ff ff 82 9b ff ff 91 ff
  //   ff 12 93 9f ff 38 8e ff
endmodule

module registers (
  input  [7:0] DATA4,
  input  WB4,
  input  [7:0] DATA3,
  input  WB3,
  input  [7:0] DATA1,
  input  WB1,
  input  CLK,
  input  [1:0] RA1,
  input  [1:0] RA3,
  input  [1:0] RA4,
  input  [1:0] RB1,
  input  [1:0] RB2,
  input  [1:0] RB3,
  input  [1:0] RB4,
  input  [1:0] RA1WB,
  input  R,
  input  [1:0] RA3WB,
  input  [1:0] RA4WB,
  input  [1:0] RA2,
  input  IMMSRC_C,
  input  B,
  input  REGW1,
  input  REGW3,
  input  REGW4,
  output [7:0] SRA1,
  output [7:0] SRB1,
  output [7:0] SRA2,
  output [7:0] SRB2,
  output [7:0] SRA3,
  output [7:0] SRB3,
  output [7:0] SRA4,
  output [7:0] SRB4,
  output L
);

  wire and_5_out, and_6_out, and_7_out, and_8_out, and_9_out, and_10_out, and_11_out, and_12_out, and_13_out,
       and_14_out, and_15_out, and_16_out, and_17_out, and_18_out, and_19_out, and_20_out, counter_1_q,
       counter_2_q, counter_3_q, counter_4_q, demultiplexer_2_out0, demultiplexer_2_out1,
       demultiplexer_2_out2, demultiplexer_2_out3, demultiplexer_3_out0, demultiplexer_3_out1,
       demultiplexer_3_out2, demultiplexer_3_out3, demultiplexer_5_out0, demultiplexer_5_out1,
       demultiplexer_5_out2, demultiplexer_5_out3, demultiplexer_6_out0, demultiplexer_6_out1,
       demultiplexer_6_out2, demultiplexer_6_out3, demultiplexer_8_out0, demultiplexer_8_out1,
       demultiplexer_8_out2, demultiplexer_8_out3, demultiplexer_9_out0, demultiplexer_9_out1,
       demultiplexer_9_out2, demultiplexer_9_out3, or_5_out, or_6_out, or_7_out, or_8_out, or_9_out,
       or_10_out, or_11_out, or_12_out, or_13_out, or_14_out, or_16_out, or_17_out, register_5_q,
       register_6_q, register_7_q, register_8_q, xor_1_out, xor_2_out, xor_3_out, xor_4_out;
  wire [1:0] RA2_t;
  wire [7:0] and_2_out, and_3_out, and_4_out, bit_extender_1_out, bit_extender_2_out, bit_extender_3_out,
       demultiplexer_1_out0, demultiplexer_1_out1, demultiplexer_1_out2, demultiplexer_1_out3,
       demultiplexer_4_out0, demultiplexer_4_out1, demultiplexer_4_out2, demultiplexer_4_out3,
       demultiplexer_7_out0, demultiplexer_7_out1, demultiplexer_7_out2, demultiplexer_7_out3, or_1_out,
       or_2_out, or_3_out, or_4_out, register_1_q, register_2_q, register_3_q, register_4_q;

  assign RA2_t = RA2 & ~{2{IMMSRC_C}};  // AND_Gate and_1, 2 bits wide
  assign bit_extender_1_out = {{7{WB4}}, WB4};  // Bit_Extender bit_extender_1
  assign bit_extender_2_out = {{7{WB3}}, WB3};  // Bit_Extender bit_extender_2
  assign bit_extender_3_out = {{7{WB1}}, WB1};  // Bit_Extender bit_extender_3
  assign and_2_out = DATA4 & bit_extender_1_out;  // AND_Gate and_2, 8 bits wide
  assign and_3_out = DATA3 & bit_extender_2_out;  // AND_Gate and_3, 8 bits wide
  assign and_4_out = DATA1 & bit_extender_3_out;  // AND_Gate and_4, 8 bits wide
  Demultiplexer #(.select(2), .width(8)) demultiplexer_1 (
    .out0(demultiplexer_1_out0), .out1(demultiplexer_1_out1), .out2(demultiplexer_1_out2),
    .out3(demultiplexer_1_out3), .in(and_4_out), .sel(RA1WB));
  Demultiplexer #(.select(2)) demultiplexer_2 (
    .out0(demultiplexer_2_out0), .out1(demultiplexer_2_out1), .out2(demultiplexer_2_out2),
    .out3(demultiplexer_2_out3), .in(WB1), .sel(RA1WB));
  Demultiplexer #(.select(2)) demultiplexer_3 (
    .out0(demultiplexer_3_out0), .out1(demultiplexer_3_out1), .out2(demultiplexer_3_out2),
    .out3(demultiplexer_3_out3), .in(REGW1), .sel(RA1));
  Demultiplexer #(.select(2), .width(8)) demultiplexer_4 (
    .out0(demultiplexer_4_out0), .out1(demultiplexer_4_out1), .out2(demultiplexer_4_out2),
    .out3(demultiplexer_4_out3), .in(and_3_out), .sel(RA3WB));
  Demultiplexer #(.select(2)) demultiplexer_5 (
    .out0(demultiplexer_5_out0), .out1(demultiplexer_5_out1), .out2(demultiplexer_5_out2),
    .out3(demultiplexer_5_out3), .in(WB3), .sel(RA3WB));
  Demultiplexer #(.select(2)) demultiplexer_6 (
    .out0(demultiplexer_6_out0), .out1(demultiplexer_6_out1), .out2(demultiplexer_6_out2),
    .out3(demultiplexer_6_out3), .in(REGW3), .sel(RA3));
  Demultiplexer #(.select(2), .width(8)) demultiplexer_7 (
    .out0(demultiplexer_7_out0), .out1(demultiplexer_7_out1), .out2(demultiplexer_7_out2),
    .out3(demultiplexer_7_out3), .in(and_2_out), .sel(RA4WB));
  Demultiplexer #(.select(2)) demultiplexer_8 (
    .out0(demultiplexer_8_out0), .out1(demultiplexer_8_out1), .out2(demultiplexer_8_out2),
    .out3(demultiplexer_8_out3), .in(WB4), .sel(RA4WB));
  Demultiplexer #(.select(2)) demultiplexer_9 (
    .out0(demultiplexer_9_out0), .out1(demultiplexer_9_out1), .out2(demultiplexer_9_out2),
    .out3(demultiplexer_9_out3), .in(REGW4), .sel(RA4));
  assign or_1_out = demultiplexer_7_out0 | demultiplexer_4_out0 | demultiplexer_1_out0;  // OR_Gate or_1, 8 bits wide
  assign or_2_out = demultiplexer_7_out1 | demultiplexer_4_out1 | demultiplexer_1_out1;  // OR_Gate or_2, 8 bits wide
  assign or_3_out = demultiplexer_7_out2 | demultiplexer_4_out2 | demultiplexer_1_out2;  // OR_Gate or_3, 8 bits wide
  assign or_4_out = demultiplexer_7_out3 | demultiplexer_4_out3 | demultiplexer_1_out3;  // OR_Gate or_4, 8 bits wide
  or or_5 (or_5_out, demultiplexer_3_out3, demultiplexer_6_out3, demultiplexer_9_out3);
  and and_5 (and_5_out, or_5_out, ~L);  // AND_Gate
  or or_6 (or_6_out, demultiplexer_3_out2, demultiplexer_6_out2, demultiplexer_9_out2);
  and and_6 (and_6_out, or_6_out, ~L);  // AND_Gate
  or or_7 (or_7_out, demultiplexer_3_out1, demultiplexer_6_out1, demultiplexer_9_out1);
  and and_7 (and_7_out, or_7_out, ~L);  // AND_Gate
  or or_8 (or_8_out, demultiplexer_3_out0, demultiplexer_6_out0, demultiplexer_9_out0);
  and and_8 (and_8_out, or_8_out, ~L);  // AND_Gate
  Register #(.trigger("falling")) register_1 (.D(or_1_out), .en(or_9_out), .clk(CLK), .Q(register_1_q), .clr(R));
  Register #(.trigger("falling")) register_2 (.D(or_2_out), .en(or_10_out), .clk(CLK), .Q(register_2_q), .clr(R));
  Register #(.trigger("falling")) register_3 (.D(or_3_out), .en(or_11_out), .clk(CLK), .Q(register_3_q), .clr(R));
  Register #(.trigger("falling")) register_4 (.D(or_4_out), .en(or_12_out), .clk(CLK), .Q(register_4_q), .clr(R));
  or or_9 (or_9_out, demultiplexer_2_out0, demultiplexer_5_out0, demultiplexer_8_out0);
  or or_10 (or_10_out, demultiplexer_2_out1, demultiplexer_5_out1, demultiplexer_8_out1);
  or or_11 (or_11_out, demultiplexer_2_out2, demultiplexer_5_out2, demultiplexer_8_out2);
  or or_12 (or_12_out, demultiplexer_2_out3, demultiplexer_5_out3, demultiplexer_8_out3);
  Register #(.trigger("low"), .width(1)) register_5 (.D(and_5_out), .en(1'b1), .Q(register_5_q), .clk(CLK), .clr(R));
  Register #(.trigger("low"), .width(1)) register_6 (.D(and_6_out), .en(1'b1), .Q(register_6_q), .clk(CLK), .clr(R));
  Register #(.trigger("low"), .width(1)) register_7 (.D(and_7_out), .en(1'b1), .Q(register_7_q), .clk(CLK), .clr(R));
  Register #(.trigger("low"), .width(1)) register_8 (.D(and_8_out), .en(1'b1), .Q(register_8_q), .clk(CLK), .clr(R));
  Multiplexer #(.select(2), .width(8)) multiplexer_1 (
    .in0(register_1_q), .in1(register_2_q), .in2(register_3_q), .in3(register_4_q), .out(SRA1), .sel(RA1));
  Multiplexer #(.select(2), .width(8)) multiplexer_2 (
    .in0(register_1_q), .in1(register_2_q), .in2(register_3_q), .in3(register_4_q), .out(SRB1), .sel(RB1));
  Multiplexer #(.select(2), .width(8)) multiplexer_3 (
    .in0(register_1_q), .in1(register_2_q), .in2(register_3_q), .in3(register_4_q), .out(SRA2), .sel(RA2_t));
  Multiplexer #(.select(2), .width(8)) multiplexer_4 (
    .in0(register_1_q), .in1(register_2_q), .in2(register_3_q), .in3(register_4_q), .out(SRB2), .sel(RB2));
  Multiplexer #(.select(2), .width(8)) multiplexer_5 (
    .in0(register_1_q), .in1(register_2_q), .in2(register_3_q), .in3(register_4_q), .out(SRA3), .sel(RA3));
  Multiplexer #(.select(2), .width(8)) multiplexer_6 (
    .in0(register_1_q), .in1(register_2_q), .in2(register_3_q), .in3(register_4_q), .out(SRB3), .sel(RB3));
  Multiplexer #(.select(2), .width(8)) multiplexer_7 (
    .in0(register_1_q), .in1(register_2_q), .in2(register_3_q), .in3(register_4_q), .out(SRA4), .sel(RA4));
  Multiplexer #(.select(2), .width(8)) multiplexer_8 (
    .in0(register_1_q), .in1(register_2_q), .in2(register_3_q), .in3(register_4_q), .out(SRB4), .sel(RB4));
  xor xor_1 (xor_1_out, or_12_out, register_5_q);
  xor xor_2 (xor_2_out, or_11_out, register_6_q);
  xor xor_3 (xor_3_out, or_10_out, register_7_q);
  xor xor_4 (xor_4_out, or_9_out, register_8_q);
  Counter #(.max('h1), .trigger("falling"), .width(1)) counter_1 (
    .count(xor_1_out), .Q(counter_1_q), .up(register_5_q), .clk(CLK), .clr(R));  // open: load, D, carry
  Counter #(.max('h1), .trigger("falling"), .width(1)) counter_2 (
    .count(xor_2_out), .Q(counter_2_q), .up(register_6_q), .clk(CLK), .clr(R));  // open: load, D, carry
  Counter #(.max('h1), .trigger("falling"), .width(1)) counter_3 (
    .count(xor_3_out), .Q(counter_3_q), .up(register_7_q), .clk(CLK), .clr(R));  // open: load, D, carry
  Counter #(.max('h1), .trigger("falling"), .width(1)) counter_4 (
    .count(xor_4_out), .Q(counter_4_q), .up(register_8_q), .clk(CLK), .clr(R));  // open: load, D, carry
  and and_9 (and_9_out, RA2_t[0], RA2_t[1], B);
  or or_13 (or_13_out, and_9_out, and_17_out);
  and and_10 (and_10_out, or_13_out, counter_1_q);
  and and_11 (and_11_out, ~RA2_t[0], RA2_t[1], B);  // AND_Gate
  or or_14 (or_14_out, and_11_out, and_18_out);
  and and_12 (and_12_out, or_14_out, counter_2_q);
  or or_15 (L, and_10_out, and_12_out, and_13_out, and_15_out);
  and and_13 (and_13_out, counter_3_q, or_16_out);
  and and_14 (and_14_out, RA2_t[0], ~RA2_t[1], B);  // AND_Gate
  or or_16 (or_16_out, and_14_out, and_19_out);
  and and_15 (and_15_out, counter_4_q, or_17_out);
  and and_16 (and_16_out, ~RA2_t[0], ~RA2_t[1], B);  // AND_Gate
  or or_17 (or_17_out, and_16_out, and_20_out);
  and and_17 (and_17_out, RB2[0], RB2[1], ~IMMSRC_C);  // AND_Gate
  and and_18 (and_18_out, ~RB2[0], RB2[1], ~IMMSRC_C);  // AND_Gate
  and and_19 (and_19_out, RB2[0], ~RB2[1], ~IMMSRC_C);  // AND_Gate
  and and_20 (and_20_out, ~RB2[0], ~RB2[1], ~IMMSRC_C);  // AND_Gate

  // Other names for the same wires on the sheet: H = L; RA1W[1:0] = RA1WB; RA3W[1:0] = RA3WB; RA4W[1:0] = RA4WB
endmodule

module ula (
  input  [7:0] RAOUT,
  input  [7:0] RBOUT,
  input  [2:0] ULAOUT,
  output [7:0] ULARES
);

  wire or_1_out;
  wire [7:0] adder_1_out, and_1_out, multiplexer_1_out, multiplexer_2_out, not_1_out, or_2_out,
       shifter_1_out, shifter_2_out, subtractor_1_out;

  Shifter #(.shift("lr")) shifter_1 (.in(RAOUT), .\dist (RBOUT[2:0]), .out(shifter_1_out));
  Multiplexer #(.width(8)) multiplexer_1 (
    .in0(shifter_1_out), .in1({8{1'b0}}), .out(multiplexer_1_out), .sel(or_1_out));
  or or_1 (or_1_out, RBOUT[3], RBOUT[4], RBOUT[5], RBOUT[6], RBOUT[7]);
  Shifter shifter_2 (.in(RAOUT), .\dist (RBOUT[2:0]), .out(shifter_2_out));
  Multiplexer #(.width(8)) multiplexer_2 (
    .in0(shifter_2_out), .in1({8{1'b0}}), .out(multiplexer_2_out), .sel(or_1_out));
  assign or_2_out = RAOUT | RBOUT;  // OR_Gate or_2, 8 bits wide
  assign and_1_out = RAOUT & RBOUT;  // AND_Gate and_1, 8 bits wide
  assign not_1_out = ~RBOUT;  // NOT_Gate not_1, 8 bits wide
  Adder adder_1 (.a(RAOUT), .b(RBOUT), .out(adder_1_out));  // open: cin, cout
  Subtractor subtractor_1 (.a(RAOUT), .b(RBOUT), .out(subtractor_1_out));  // open: bin, bout
  Multiplexer #(.select(3), .width(8)) multiplexer_3 (
    .in0(adder_1_out), .in1(subtractor_1_out), .in2(and_1_out), .in3(or_2_out), .in4(not_1_out),
    .in5(multiplexer_2_out), .in6(multiplexer_1_out), .in7({8{1'b0}}), .out(ULARES), .sel(ULAOUT));
endmodule

module control (
  input  [3:0] OPCODE1,
  input  [3:0] OPCODE2,
  input  [3:0] OPCODE3,
  input  [3:0] OPCODE4,
  output [1:0] MOV,
  output IMMSRC_D,
  output REGW1,
  output MEMWRITE,
  output [1:0] PCSRC,
  output IMMSRC_C,
  output B,
  output [2:0] ULAOUT3,
  output REGW3,
  output [2:0] ULAOUT4,
  output REGW4
);

  wire and_2_out;

  and and_1 (MOV[0], OPCODE1[0], OPCODE1[1]);
  and and_2 (and_2_out, OPCODE1[1], ~OPCODE1[3]);  // AND_Gate
  not not_1 (B, OPCODE2[1]);
  or or_1 (REGW1, ~OPCODE1[0], and_2_out);  // OR_Gate
  and and_3 (MEMWRITE, OPCODE1[0], ~OPCODE1[1]);  // AND_Gate
  and and_4 (PCSRC[0], OPCODE2[0], ~OPCODE2[2]);  // AND_Gate
  and and_5 (PCSRC[1], ~OPCODE2[2], ~OPCODE2[0]);  // AND_Gate
  or or_2 (REGW3, ~OPCODE3[2], ~OPCODE3[1], ~OPCODE3[0]);  // OR_Gate
  or or_3 (REGW4, ~OPCODE4[2], ~OPCODE4[1], ~OPCODE4[0]);  // OR_Gate

  assign IMMSRC_C = OPCODE2[0];
  assign IMMSRC_D = OPCODE1[1];
  assign MOV[1] = OPCODE1[1];
  assign ULAOUT3 = OPCODE3[2:0];
  assign ULAOUT4 = OPCODE4[2:0];
endmodule

module Zero (
  input  [7:0] S,
  output Zero
);

  wire or_1_out, or_2_out;

  or or_1 (or_1_out, S[0], S[1], S[2], S[3]);
  or or_2 (or_2_out, S[4], S[5], S[6], S[7]);
  nor nor_1 (Zero, or_1_out, or_2_out);
endmodule

module forwardingUnit (
  input  [7:0] SRA1_A,
  input  [7:0] SRA3_A,
  input  [7:0] SRA4_A,
  input  [1:0] RA1_B,
  input  WRA1_A,
  input  [1:0] RA1_A,
  input  WRA3_A,
  input  [1:0] RA3_A,
  input  WRA4_A,
  input  [1:0] RA4_A,
  input  [1:0] RA3_B,
  input  [1:0] RA4_B,
  input  [1:0] RB1_B,
  input  [1:0] RB3_B,
  input  [1:0] RB4_B,
  output DepRA1,
  output [7:0] SRA1,
  output DepRA3,
  output [7:0] SRA3,
  output DepRA4,
  output [7:0] SRA4,
  output DepRB1,
  output [7:0] SRB1,
  output DepRB3,
  output [7:0] SRB3,
  output DepRB4,
  output [7:0] SRB4
);

  wire and_1_out, and_2_out, and_3_out, and_4_out, and_5_out, and_6_out, and_7_out, and_8_out, and_9_out,
       and_10_out, and_11_out, and_12_out, and_13_out, and_14_out, and_15_out, and_16_out, and_17_out,
       and_18_out, equal_1_s, equal_2_s, equal_3_s, equal_4_s, equal_5_s, equal_6_s, equal_7_s, equal_8_s,
       equal_9_s, equal_10_s, equal_11_s, equal_12_s, equal_13_s, equal_14_s, equal_15_s, equal_16_s,
       equal_17_s, equal_18_s;
  wire [7:0] and_19_out, and_20_out, and_21_out, and_22_out, and_23_out, and_24_out, and_25_out, and_26_out,
       and_27_out, and_28_out, and_29_out, and_30_out, and_31_out, and_32_out, and_33_out, and_34_out,
       and_35_out, and_36_out, bit_extender_1_out, bit_extender_2_out, bit_extender_3_out,
       bit_extender_4_out, bit_extender_5_out, bit_extender_6_out, bit_extender_7_out, bit_extender_8_out,
       bit_extender_9_out, bit_extender_10_out, bit_extender_11_out, bit_extender_12_out,
       bit_extender_13_out, bit_extender_14_out, bit_extender_15_out, bit_extender_16_out,
       bit_extender_17_out, bit_extender_18_out;

  equal equal_1 (.E1(RA1_A), .E2(RA1_B), .S(equal_1_s));
  equal equal_2 (.E1(RA3_A), .E2(RA1_B), .S(equal_2_s));
  equal equal_3 (.E1(RA4_A), .E2(RA1_B), .S(equal_3_s));
  equal equal_4 (.E1(RA1_A), .E2(RA3_B), .S(equal_4_s));
  equal equal_5 (.E1(RA3_A), .E2(RA3_B), .S(equal_5_s));
  equal equal_6 (.E1(RA4_A), .E2(RA3_B), .S(equal_6_s));
  equal equal_7 (.E1(RA1_A), .E2(RA4_B), .S(equal_7_s));
  equal equal_8 (.E1(RA3_A), .E2(RA4_B), .S(equal_8_s));
  equal equal_9 (.E1(RA4_A), .E2(RA4_B), .S(equal_9_s));
  equal equal_10 (.E1(RA1_A), .E2(RB1_B), .S(equal_10_s));
  equal equal_11 (.E1(RA3_A), .E2(RB1_B), .S(equal_11_s));
  equal equal_12 (.E1(RA4_A), .E2(RB1_B), .S(equal_12_s));
  equal equal_13 (.E1(RA1_A), .E2(RB3_B), .S(equal_13_s));
  equal equal_14 (.E1(RA3_A), .E2(RB3_B), .S(equal_14_s));
  equal equal_15 (.E1(RA4_A), .E2(RB3_B), .S(equal_15_s));
  equal equal_16 (.E1(RA1_A), .E2(RB4_B), .S(equal_16_s));
  equal equal_17 (.E1(RA3_A), .E2(RB4_B), .S(equal_17_s));
  equal equal_18 (.E1(RA4_A), .E2(RB4_B), .S(equal_18_s));
  and and_1 (and_1_out, WRA1_A, equal_1_s);
  and and_2 (and_2_out, WRA3_A, equal_2_s);
  and and_3 (and_3_out, WRA4_A, equal_3_s);
  and and_4 (and_4_out, WRA1_A, equal_4_s);
  and and_5 (and_5_out, WRA3_A, equal_5_s);
  and and_6 (and_6_out, WRA4_A, equal_6_s);
  and and_7 (and_7_out, WRA1_A, equal_7_s);
  and and_8 (and_8_out, WRA3_A, equal_8_s);
  and and_9 (and_9_out, WRA4_A, equal_9_s);
  and and_10 (and_10_out, WRA1_A, equal_10_s);
  and and_11 (and_11_out, WRA3_A, equal_11_s);
  and and_12 (and_12_out, WRA4_A, equal_12_s);
  and and_13 (and_13_out, WRA1_A, equal_13_s);
  and and_14 (and_14_out, WRA3_A, equal_14_s);
  and and_15 (and_15_out, WRA4_A, equal_15_s);
  and and_16 (and_16_out, WRA1_A, equal_16_s);
  and and_17 (and_17_out, WRA3_A, equal_17_s);
  and and_18 (and_18_out, WRA4_A, equal_18_s);
  assign bit_extender_1_out = {{7{and_1_out}}, and_1_out};  // Bit_Extender bit_extender_1
  assign bit_extender_2_out = {{7{and_2_out}}, and_2_out};  // Bit_Extender bit_extender_2
  assign bit_extender_3_out = {{7{and_3_out}}, and_3_out};  // Bit_Extender bit_extender_3
  assign bit_extender_4_out = {{7{and_4_out}}, and_4_out};  // Bit_Extender bit_extender_4
  assign bit_extender_5_out = {{7{and_5_out}}, and_5_out};  // Bit_Extender bit_extender_5
  assign bit_extender_6_out = {{7{and_6_out}}, and_6_out};  // Bit_Extender bit_extender_6
  assign bit_extender_7_out = {{7{and_7_out}}, and_7_out};  // Bit_Extender bit_extender_7
  assign bit_extender_8_out = {{7{and_8_out}}, and_8_out};  // Bit_Extender bit_extender_8
  assign bit_extender_9_out = {{7{and_9_out}}, and_9_out};  // Bit_Extender bit_extender_9
  assign bit_extender_10_out = {{7{and_10_out}}, and_10_out};  // Bit_Extender bit_extender_10
  assign bit_extender_11_out = {{7{and_11_out}}, and_11_out};  // Bit_Extender bit_extender_11
  assign bit_extender_12_out = {{7{and_12_out}}, and_12_out};  // Bit_Extender bit_extender_12
  assign bit_extender_13_out = {{7{and_13_out}}, and_13_out};  // Bit_Extender bit_extender_13
  assign bit_extender_14_out = {{7{and_14_out}}, and_14_out};  // Bit_Extender bit_extender_14
  assign bit_extender_15_out = {{7{and_15_out}}, and_15_out};  // Bit_Extender bit_extender_15
  assign bit_extender_16_out = {{7{and_16_out}}, and_16_out};  // Bit_Extender bit_extender_16
  assign bit_extender_17_out = {{7{and_17_out}}, and_17_out};  // Bit_Extender bit_extender_17
  assign bit_extender_18_out = {{7{and_18_out}}, and_18_out};  // Bit_Extender bit_extender_18
  assign and_19_out = bit_extender_1_out & SRA1_A;  // AND_Gate and_19, 8 bits wide
  assign and_20_out = bit_extender_2_out & SRA3_A;  // AND_Gate and_20, 8 bits wide
  assign and_21_out = bit_extender_3_out & SRA4_A;  // AND_Gate and_21, 8 bits wide
  assign and_22_out = bit_extender_4_out & SRA1_A;  // AND_Gate and_22, 8 bits wide
  assign and_23_out = bit_extender_5_out & SRA3_A;  // AND_Gate and_23, 8 bits wide
  assign and_24_out = bit_extender_6_out & SRA4_A;  // AND_Gate and_24, 8 bits wide
  assign and_25_out = bit_extender_7_out & SRA1_A;  // AND_Gate and_25, 8 bits wide
  assign and_26_out = bit_extender_8_out & SRA3_A;  // AND_Gate and_26, 8 bits wide
  assign and_27_out = bit_extender_9_out & SRA4_A;  // AND_Gate and_27, 8 bits wide
  assign and_28_out = bit_extender_10_out & SRA1_A;  // AND_Gate and_28, 8 bits wide
  assign and_29_out = bit_extender_11_out & SRA3_A;  // AND_Gate and_29, 8 bits wide
  assign and_30_out = bit_extender_12_out & SRA4_A;  // AND_Gate and_30, 8 bits wide
  assign and_31_out = bit_extender_13_out & SRA1_A;  // AND_Gate and_31, 8 bits wide
  assign and_32_out = bit_extender_14_out & SRA3_A;  // AND_Gate and_32, 8 bits wide
  assign and_33_out = bit_extender_15_out & SRA4_A;  // AND_Gate and_33, 8 bits wide
  assign and_34_out = bit_extender_16_out & SRA1_A;  // AND_Gate and_34, 8 bits wide
  assign and_35_out = bit_extender_17_out & SRA3_A;  // AND_Gate and_35, 8 bits wide
  assign and_36_out = bit_extender_18_out & SRA4_A;  // AND_Gate and_36, 8 bits wide
  or or_1 (DepRA1, and_1_out, and_2_out, and_3_out);
  assign SRA1 = and_19_out | and_20_out | and_21_out;  // OR_Gate or_2, 8 bits wide
  or or_3 (DepRA3, and_4_out, and_5_out, and_6_out);
  assign SRA3 = and_22_out | and_23_out | and_24_out;  // OR_Gate or_4, 8 bits wide
  or or_5 (DepRA4, and_7_out, and_8_out, and_9_out);
  assign SRA4 = and_25_out | and_26_out | and_27_out;  // OR_Gate or_6, 8 bits wide
  or or_7 (DepRB1, and_10_out, and_11_out, and_12_out);
  assign SRB1 = and_28_out | and_29_out | and_30_out;  // OR_Gate or_8, 8 bits wide
  or or_9 (DepRB3, and_13_out, and_14_out, and_15_out);
  assign SRB3 = and_31_out | and_32_out | and_33_out;  // OR_Gate or_10, 8 bits wide
  or or_11 (DepRB4, and_16_out, and_17_out, and_18_out);
  assign SRB4 = and_34_out | and_35_out | and_36_out;  // OR_Gate or_12, 8 bits wide
endmodule

module equal (
  input  [1:0] E1,
  input  [1:0] E2,
  output S
);

  wire [1:0] xor_1_out;

  assign xor_1_out = E1 ^ E2;  // XOR_Gate xor_1, 2 bits wide
  nor nor_1 (S, xor_1_out[0], xor_1_out[1]);
endmodule
